# Fritzing sketch Big (saved by Fritzing 0.9.3b)
breadboards: 1

parts:
  PART2 = Pi Wedge B+
  Raspberry_Pi_2 = Raspberry Pi 3 [part_number=RPI-3-V1.2]  # not connected
  module35 = I2C LCD1602
  module36 = LM393
  module37 = Rain Detection board
  module38 = Tilt-Switch
  module39 = Dule-Color LED
  module40 = PCF8591

nets:
  VCC: PART2.5V#39, PART2.5V#71, module35.VCC, module36.VCC, module40.VCC
  N1: PART2.G17, module36.DO
  N2: PART2.5V#54, module38.VCC
  GND: PART2.GND, module35.GND, module36.GND#8, module38.GND, module39.GND, module40.GND
  N3: PART2.G20, module39.G
  N4: PART2.G21, module39.R
  N5: PART2.G24, module38.SIG
  N6: PART2.SCL, module35.SCL, module40.SCL
  N7: PART2.SDA, module35.SDA, module40.SDA
  N8: module36.AO, module40.AIN0
  N9: module36.IN, module37.-
  N10: module36.GND#10, module37.+

custom parts:
  Pi Wedge B+: This is the Pi Wedge B Plus, a board that connects to the Raspberry Pi B+’s 40-pin GPIO connector, and breaks the pins out to breadboard-friendly arrangement and spacing, and even adds a couple of decoupling capacitors on the power supply lines. The “Wedge” also makes the initial bringup process easier - you can plug an FTDI Basic module into the built-in serial port. Each Pi Wedge comes as an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
  I2C LCD1602: I2C LCD1602 module of ZHIYU Sensor Kit
  LM393: LM393 module of ZHIYU Sensor Kit
  Rain Detection board: Rain Detection board for ZHIYU Sensor Kit (along with LM393).
  Tilt-Switch: Tilt-Switch module of ZHIYU Sensor Kit
  Dule-Color LED: DuleColor LED module of SunFounder Sensor Kit
  PCF8591: PCF8591 ADC module for SunFounder Sensor Kit
